// Logisim project RV32I.circ as structural Verilog: 15 circuits, main circuit main
module main (
  input  pc_sel
);

  wire b_sel, pc_rst_out, reg_write, sys_clk, sys_rst;
  wire [2:0] funct3;
  wire [4:0] undriven, undriven_2, undriven_3;
  wire [6:0] funct7, opcode;
  wire [31:0] adder1_sum, adder2_sum, alu1_alu_out, instr_mem_1_instr_out, multiplexer_1_out,
       multiplexer_2_out, Prog_Counter_pc_out, register_file_1_rs1_data, register_file_1_rs2_data, undriven_4;

  Button rst (.out(sys_rst));
  Clock clk (.out(sys_clk));
  Multiplexer #(.width(32)) multiplexer_1 (.in0(adder1_sum), .in1(adder2_sum), .out(multiplexer_1_out), .sel(pc_sel));
  Button pc_rst (.out(pc_rst_out));
  PC Prog_Counter (.clk(sys_clk), .rst(pc_rst_out), .pc_nxt(multiplexer_1_out), .pc_out(Prog_Counter_pc_out));
  // Probe on Prog_Counter_pc_out[9:0]
  increment adder1 (.A(Prog_Counter_pc_out), .B(32'h4), .Sum(adder1_sum));
  // Probe on instr_mem_1_instr_out
  Instr_mem instr_mem_1 (.pc(Prog_Counter_pc_out[9:0]), .instr_out(instr_mem_1_instr_out));
  Instr_Decode instr_decode_1 (
    .instr(instr_mem_1_instr_out), .opcode(opcode), .rd(undriven_3), .funct3(funct3), .rs1(undriven),
    .rs2(undriven_2), .funct7(funct7));
  increment adder2 (.A(undriven_4), .B(Prog_Counter_pc_out), .Sum(adder2_sum));
  Register_file register_file_1 (
    .rs1(undriven), .rs2(undriven_2), .rd(undriven_3), .reg_write(reg_write), .reg_clk(sys_clk),
    .rs1_data(register_file_1_rs1_data), .rs2_data(register_file_1_rs2_data));  // open: rd_data
  Multiplexer #(.width(32)) multiplexer_2 (
    .in0(register_file_1_rs2_data), .in1(undriven_4), .out(multiplexer_2_out), .sel(b_sel));
  ALU alu1 (.alu_A(register_file_1_rs1_data), .alu_B(multiplexer_2_out), .alu_out(alu1_alu_out));  // open: alu_sel
endmodule

module PC (
  input  [31:0] pc_nxt,
  input  clk,
  input  rst,
  output [31:0] pc_out
);

  wire pull_resistor_1_node;

  Pull_Resistor #(.pull(1)) pull_resistor_1 (.node(pull_resistor_1_node));
  Register #(.width(32)) pc_reg (.D(pc_nxt), .en(pull_resistor_1_node), .clk(clk), .Q(pc_out), .clr(rst));
endmodule

module increment (
  input  [31:0] A,
  input  [31:0] B,
  output [31:0] Sum
);

  wire adder_1_cout;

  Adder #(.width(32)) adder_1 (.a(A), .b(B), .out(Sum), .cin(1'b0), .cout(adder_1_cout));
  // also tied to GND on the sheet: adder_1_cout
endmodule

module Instr_mem (
  input  [9:0] pc,
  output [31:0] instr_out
);

  wire [9:0] shifter_1_out;

  Shifter #(.shift("lr"), .width(10)) shifter_1 (.in(pc), .\dist (4'b0010), .out(shifter_1_out));
  ROM #(.addrWidth(10), .dataWidth(32)) mem (.addr(shifter_1_out), .data(instr_out));
endmodule

module R_Splitter (
  input  [31:0] instr,
  output [6:0] opcode,
  output [4:0] rd,
  output [2:0] funct3,
  output [4:0] rs1,
  output [4:0] rs2,
  output [6:0] funct7
);


  assign funct3 = instr[14:12];
  assign funct7 = instr[31:25];
  assign opcode = instr[6:0];
  assign rd = instr[11:7];
  assign rs1 = instr[19:15];
  assign rs2 = instr[24:20];
endmodule

module I_Splitter (
  input  [31:0] instr,
  output [6:0] opcode,
  output [4:0] rd,
  output [2:0] funct3,
  output [4:0] rs1,
  output [11:0] imm_i
);


  assign funct3 = instr[14:12];
  assign imm_i = instr[31:20];
  assign opcode = instr[6:0];
  assign rd = instr[11:7];
  assign rs1 = instr[19:15];
endmodule

module S_Splitter (
  input  [31:0] instr,
  output [6:0] opcode,
  output [2:0] funct3,
  output [4:0] rs1,
  output [4:0] rs2,
  output [11:0] imm_s
);


  assign funct3 = instr[14:12];
  assign imm_s = {instr[31:25], instr[11:7]};
  assign opcode = instr[6:0];
  assign rs1 = instr[19:15];
  assign rs2 = instr[24:20];
endmodule

module B_Splitter (
  input  [31:0] instr,
  output [6:0] opcode,
  output [2:0] funct3,
  output [4:0] rs1,
  output [4:0] rs2,
  output [12:0] imm_s
);


  assign funct3 = instr[14:12];
  assign imm_s = {instr[31:25], instr[11:7], 1'b0};
  assign opcode = instr[6:0];
  assign rs1 = instr[19:15];
  assign rs2 = instr[24:20];
endmodule

module U_Splitter (
  input  [31:0] instr,
  output [6:0] opcode,
  output [4:0] rd,
  output [19:0] imm_i
);


  assign imm_i = instr[31:12];
  assign opcode = instr[6:0];
  assign rd = instr[11:7];
endmodule

module J_Splitter (
  input  [31:0] instr,
  output [6:0] opcode,
  output [4:0] rd,
  output [19:0] imm_i
);


  assign imm_i = instr[31:12];
  assign opcode = instr[6:0];
  assign rd = instr[11:7];
endmodule

module ALU (
  input  [31:0] alu_A,
  input  [31:0] alu_B,
  input  [3:0] alu_sel,
  output [31:0] alu_out
);

  wire adder_1_cout, comparator_1_lt, comparator_2_lt, subtractor_1_bout;
  wire [31:0] addOut, andOut, orOut, sllOut, sltOut, sltuOut, sraOut, srlOut, subOut, xorOut;

  // NoConnect on adder_1_cout
  // NoConnect on subtractor_1_bout
  Adder #(.width(32)) adder_1 (.a(alu_A), .b(alu_B), .out(addOut), .cin(1'b0), .cout(adder_1_cout));
  Subtractor #(.width(32)) subtractor_1 (.a(alu_A), .b(alu_B), .out(subOut), .bin(1'b0), .bout(subtractor_1_bout));
  assign xorOut = alu_A ^ alu_B;  // XOR_Gate xor_1, 32 bits wide
  assign orOut = alu_A | alu_B;  // OR_Gate or_1, 32 bits wide
  assign andOut = alu_A & alu_B;  // AND_Gate and_1, 32 bits wide
  Shifter #(.width(32)) shifter_1 (.in(alu_A), .\dist (alu_B[4:0]), .out(sllOut));
  Shifter #(.shift("lr"), .width(32)) shifter_2 (.in(alu_A), .\dist (alu_B[4:0]), .out(srlOut));
  Shifter #(.shift("ar"), .width(32)) shifter_3 (.in(alu_A), .\dist (alu_B[4:0]), .out(sraOut));
  Comparator #(.width(32)) comparator_1 (.a(alu_A), .b(alu_B), .lt(comparator_1_lt));  // open: gt, eq
  Comparator #(.mode("unsigned"), .width(32)) comparator_2 (
    .a(alu_A), .b(alu_B), .lt(comparator_2_lt));  // open: gt, eq
  assign sltOut = {{31{1'b0}}, comparator_1_lt};  // Bit_Extender bit_extender_1
  assign sltuOut = {{31{1'b0}}, comparator_2_lt};  // Bit_Extender bit_extender_2
  Multiplexer #(.select(4), .width(32)) multiplexer_1 (
    .in0(addOut), .in1(subOut), .in2(xorOut), .in3(orOut), .in4(andOut), .in5(sllOut), .in6(srlOut),
    .in7(sraOut), .in8(sltOut), .in9(sltuOut), .in10({32{1'b0}}), .in11({32{1'b0}}), .in12({32{1'b0}}),
    .in13({32{1'b0}}), .in14({32{1'b0}}), .in15({32{1'b0}}), .out(alu_out), .sel(alu_sel));

  // Notes on the sheet:
  //   RV32I ALU Operations
  //   Sel - 4 bits
  //   0000 - ADD
  //   0001 - SUB
  //   0010 - XOR
  //   0011 - OR
  //   0100 - AND
  //   1000 - SLT (Set Less Than)
  //   0101 - SLL (Shift Left Logical)
  //   0110 - SRL (Shift Right Logical)
  //   0111 - SRA (Shift Right Arithmetic)
  //   1001 - SLTU (Set Less Than Unsigned)
endmodule

module Register_file (
  input  [4:0] rs1,
  input  [4:0] rs2,
  input  [4:0] rd,
  input  [31:0] rd_data,
  input  reg_write,
  input  reg_clk,
  output [31:0] rs1_data,
  output [31:0] rs2_data
);

  wire x0_we, x1_we, x2_we, x3_we, x4_we, x5_we, x6_we, x7_we, x8_we, x9_we, x10_we, x11_we, x12_we, x13_we,
       x14_we, x15_we, x16_we, x17_we, x18_we, x19_we, x20_we, x21_we, x22_we, x23_we, x24_we, x25_we,
       x26_we, x27_we, x28_we, x29_we, x30_we, x31_we;
  wire [31:0] x1_q, x2_q, x2_q2, x3_q, x3_q3, x4_q, x5_q, x6_q, x7_q, x8_q, x9_q, x10_q, x11_q, x12_q, x13_q,
       x14_q, x15_q, x16_q, x17_q, x18_q, x19_q, x20_q, x21_q, x22_q, x23_q, x24_q, x25_q, x26_q, x27_q,
       x28_q, x29_q, x30_q, x31_q;

  Demultiplexer #(.select(5)) demultiplexer_1 (
    .out0(x0_we), .out1(x1_we), .out2(x2_we), .out3(x3_we), .out4(x4_we), .out5(x5_we), .out6(x6_we),
    .out7(x7_we), .out8(x8_we), .out9(x9_we), .out10(x10_we), .out11(x11_we), .out12(x12_we), .out13(x13_we),
    .out14(x14_we), .out15(x15_we), .out16(x16_we), .out17(x17_we), .out18(x18_we), .out19(x19_we),
    .out20(x20_we), .out21(x21_we), .out22(x22_we), .out23(x23_we), .out24(x24_we), .out25(x25_we),
    .out26(x26_we), .out27(x27_we), .out28(x28_we), .out29(x29_we), .out30(x30_we), .out31(x31_we),
    .in(reg_write), .sel(rd));
  Register #(.width(32)) x4 (.D(rd_data), .en(x4_we), .clk(reg_clk), .Q(x4_q));  // open: clr
  Register #(.width(32)) x8 (.D(rd_data), .en(x8_we), .clk(reg_clk), .Q(x8_q));  // open: clr
  Register #(.width(32)) x12 (.D(rd_data), .en(x12_we), .clk(reg_clk), .Q(x12_q));  // open: clr
  Register #(.width(32)) x16 (.D(rd_data), .en(x16_we), .clk(reg_clk), .Q(x16_q));  // open: clr
  Register #(.width(32)) x20 (.D(rd_data), .en(x20_we), .clk(reg_clk), .Q(x20_q));  // open: clr
  Register #(.width(32)) x24 (.D(rd_data), .en(x24_we), .clk(reg_clk), .Q(x24_q));  // open: clr
  Register #(.width(32)) x28 (.D(rd_data), .en(x28_we), .clk(reg_clk), .Q(x28_q));  // open: clr
  Register #(.width(32)) x1 (.D(rd_data), .en(x1_we), .clk(reg_clk), .Q(x1_q));  // open: clr
  Register #(.width(32)) x5 (.D(rd_data), .en(x5_we), .clk(reg_clk), .Q(x5_q));  // open: clr
  Register #(.width(32)) x9 (.D(rd_data), .en(x9_we), .clk(reg_clk), .Q(x9_q));  // open: clr
  Register #(.width(32)) x13 (.D(rd_data), .en(x13_we), .clk(reg_clk), .Q(x13_q));  // open: clr
  Register #(.width(32)) x17 (.D(rd_data), .en(x17_we), .clk(reg_clk), .Q(x17_q));  // open: clr
  Register #(.width(32)) x21 (.D(rd_data), .en(x21_we), .clk(reg_clk), .Q(x21_q));  // open: clr
  Register #(.width(32)) x25 (.D(rd_data), .en(x25_we), .clk(reg_clk), .Q(x25_q));  // open: clr
  Register #(.width(32)) x29 (.D(rd_data), .en(x29_we), .clk(reg_clk), .Q(x29_q));  // open: clr
  Register #(.width(32)) x2 (.D(rd_data), .en(x2_we), .clk(reg_clk), .Q(x2_q2));  // open: clr
  Register #(.width(32)) x6 (.D(rd_data), .en(x6_we), .clk(reg_clk), .Q(x6_q));  // open: clr
  Register #(.width(32)) x10 (.D(rd_data), .en(x10_we), .clk(reg_clk), .Q(x10_q));  // open: clr
  Register #(.width(32)) x14 (.D(rd_data), .en(x14_we), .clk(reg_clk), .Q(x14_q));  // open: clr
  Register #(.width(32)) x18 (.D(rd_data), .en(x18_we), .clk(reg_clk), .Q(x18_q));  // open: clr
  Register #(.width(32)) x22 (.D(rd_data), .en(x22_we), .clk(reg_clk), .Q(x22_q));  // open: clr
  Register #(.width(32)) x26 (.D(rd_data), .en(x26_we), .clk(reg_clk), .Q(x26_q));  // open: clr
  Register #(.width(32)) x30 (.D(rd_data), .en(x30_we), .clk(reg_clk), .Q(x30_q));  // open: clr
  Register #(.width(32)) x3 (.D(rd_data), .en(x3_we), .clk(reg_clk), .Q(x3_q3));  // open: clr
  Register #(.width(32)) x7 (.D(rd_data), .en(x7_we), .clk(reg_clk), .Q(x7_q));  // open: clr
  Register #(.width(32)) x11 (.D(rd_data), .en(x11_we), .clk(reg_clk), .Q(x11_q));  // open: clr
  Register #(.width(32)) x15 (.D(rd_data), .en(x15_we), .clk(reg_clk), .Q(x15_q));  // open: clr
  Register #(.width(32)) x19 (.D(rd_data), .en(x19_we), .clk(reg_clk), .Q(x19_q));  // open: clr
  Register #(.width(32)) x23 (.D(rd_data), .en(x23_we), .clk(reg_clk), .Q(x23_q));  // open: clr
  Register #(.width(32)) x27 (.D(rd_data), .en(x27_we), .clk(reg_clk), .Q(x27_q));  // open: clr
  Register #(.width(32)) x31 (.D(rd_data), .en(x31_we), .clk(reg_clk), .Q(x31_q));  // open: clr
  Multiplexer #(.select(5), .width(32)) multiplexer_1 (
    .in0({32{1'b0}}), .in1(x1_q), .in2(x2_q), .in3(x3_q), .in4(x4_q), .in5(x5_q), .in6(x6_q), .in7(x7_q),
    .in8(x8_q), .in9(x9_q), .in10(x10_q), .in11(x11_q), .in12(x12_q), .in13(x13_q), .in14(x14_q),
    .in15(x15_q), .in16(x16_q), .in17(x17_q), .in18(x18_q), .in19(x19_q), .in20(x20_q), .in21(x21_q),
    .in22(x22_q), .in23(x23_q), .in24(x24_q), .in25(x25_q), .in26(x26_q), .in27(x27_q), .in28(x28_q),
    .in29(x29_q), .in30(x30_q), .in31(x31_q), .out(rs1_data), .sel(rs1));
  Multiplexer #(.select(5), .width(32)) multiplexer_2 (
    .in0({32{1'b0}}), .in1(x1_q), .in2(x2_q), .in3(x3_q), .in4(x4_q), .in5(x5_q), .in6(x6_q), .in7(x7_q),
    .in8(x8_q), .in9(x9_q), .in10(x10_q), .in11(x11_q), .in12(x12_q), .in13(x13_q), .in14(x14_q),
    .in15(x15_q), .in16(x16_q), .in17(x17_q), .in18(x18_q), .in19(x19_q), .in20(x20_q), .in21(x21_q),
    .in22(x22_q), .in23(x23_q), .in24(x24_q), .in25(x25_q), .in26(x26_q), .in27(x27_q), .in28(x28_q),
    .in29(x29_q), .in30(x30_q), .in31(x31_q), .out(rs2_data), .sel(rs2));
endmodule

module Imm_gen (
  input  [31:0] instr_in,
  output [31:0] out_2,
  output [31:0] imm_out
);

  wire b_id, comparator_1_eq, comparator_2_eq, comparator_3_eq, comparator_6_eq, comparator_7_eq, i_id, j_id,
       s_id, u_id;
  wire [2:0] B_split_funct3, I_split_funct3, imm_sel, S_split_funct3;
  wire [4:0] B_split_rs1, B_split_rs2, I_split_rd, I_split_rs1, J_split_rd, S_split_rs1, S_split_rs2,
       U_split_rd;
  wire [6:0] B_opcode, I_opcode, J_opcode, S_opcode, U_opcode;
  wire [11:0] imm_I, imm_S;
  wire [12:0] imm_B;
  wire [19:0] imm_J, imm_U;
  wire [31:0] bit_extender_1_out, bit_extender_2_out, bit_extender_3_out, bit_extender_4_out,
       bit_extender_5_out;

  I_Splitter I_split (
    .instr(instr_in), .opcode(I_opcode), .rd(I_split_rd), .funct3(I_split_funct3), .rs1(I_split_rs1),
    .imm_i(imm_I));
  // NoConnect on I_split_rd
  // NoConnect on I_split_funct3
  // NoConnect on I_split_rs1
  S_Splitter S_split (
    .instr(instr_in), .opcode(S_opcode), .funct3(S_split_funct3), .rs1(S_split_rs1), .rs2(S_split_rs2),
    .imm_s(imm_S));
  // NoConnect on S_split_funct3
  // NoConnect on S_split_rs1
  // NoConnect on S_split_rs2
  B_Splitter B_split (
    .instr(instr_in), .opcode(B_opcode), .funct3(B_split_funct3), .rs1(B_split_rs1), .rs2(B_split_rs2),
    .imm_s(imm_B));
  // NoConnect on B_split_funct3
  // NoConnect on B_split_rs1
  // NoConnect on B_split_rs2
  U_Splitter U_split (.instr(instr_in), .opcode(U_opcode), .rd(U_split_rd), .imm_i(imm_U));
  // NoConnect on U_split_rd
  J_Splitter J_split (.instr(instr_in), .opcode(J_opcode), .rd(J_split_rd), .imm_i(imm_J));
  // NoConnect on J_split_rd
  Comparator #(.mode("unsigned"), .width(7)) comparator_1 (
    .a(I_opcode), .b(7'b0010011), .eq(comparator_1_eq));  // open: gt, lt
  Comparator #(.mode("unsigned"), .width(7)) comparator_2 (
    .a(I_opcode), .b(7'b0000011), .eq(comparator_2_eq));  // open: gt, lt
  Comparator #(.mode("unsigned"), .width(7)) comparator_3 (
    .a(I_opcode), .b(7'b1100111), .eq(comparator_3_eq));  // open: gt, lt
  Comparator #(.mode("unsigned"), .width(7)) comparator_4 (.a(S_opcode), .b(7'b0100011), .eq(s_id));  // open: gt, lt
  Comparator #(.mode("unsigned"), .width(7)) comparator_5 (.a(B_opcode), .b(7'b1100011), .eq(b_id));  // open: gt, lt
  Comparator #(.mode("unsigned"), .width(7)) comparator_6 (
    .a(U_opcode), .b(7'b0110111), .eq(comparator_6_eq));  // open: gt, lt
  Comparator #(.mode("unsigned"), .width(7)) comparator_7 (
    .a(U_opcode), .b(7'b0010111), .eq(comparator_7_eq));  // open: gt, lt
  Comparator #(.mode("unsigned"), .width(7)) comparator_8 (.a(J_opcode), .b(7'b1101111), .eq(j_id));  // open: gt, lt
  or I_or (i_id, comparator_1_eq, comparator_2_eq, comparator_3_eq);
  or U_or (u_id, comparator_6_eq, comparator_7_eq);
  assign bit_extender_1_out = {{20{imm_I[11]}}, imm_I};  // Bit_Extender bit_extender_1
  assign bit_extender_2_out = {{20{imm_S[11]}}, imm_S};  // Bit_Extender bit_extender_2
  assign bit_extender_3_out = {{19{imm_B[12]}}, imm_B};  // Bit_Extender bit_extender_3
  assign bit_extender_4_out = {{12{imm_U[19]}}, imm_U};  // Bit_Extender bit_extender_4
  assign bit_extender_5_out = {{12{imm_J[19]}}, imm_J};  // Bit_Extender bit_extender_5
  ROM #(.addrWidth(5), .dataWidth(3)) rom_1 (.addr({j_id, u_id, b_id, s_id, i_id}), .data(imm_sel));
  Multiplexer #(.select(3), .width(32)) multiplexer_1 (
    .in0(bit_extender_1_out), .in1(bit_extender_2_out), .in2(bit_extender_3_out), .in3(bit_extender_4_out),
    .in4(bit_extender_5_out), .in5({32{1'b0}}), .in6({32{1'b0}}), .in7({32{1'b0}}), .out(imm_out),
    .sel(imm_sel));

  // Notes on the sheet:
  //   contents of rom_1 (hex, n*v repeats v):
  //   0 0 1 2 3 4 5
endmodule

module Instr_Decode (
  input  [6:0] opcode,
  input  [4:0] rd,
  input  [2:0] funct3,
  input  [4:0] rs1,
  input  [4:0] rs2,
  input  [6:0] funct7,
  input  [31:0] instr
);


  assign {instr[31:25], instr[14:12]} = {funct7, funct3};
  assign opcode = instr[6:0];
  assign rd = instr[11:7];
  assign rs1 = instr[19:15];
  assign rs2 = instr[24:20];
endmodule

module Data_mem (
  input  [9:0] in_1,
  output [31:0] out_2
);

  wire clock_1_out;

  RAM #(.addrWidth(10), .asyncread("true"), .byteenables("byteEnables"), .dataWidth(32)) ram_1 (
    .addr(in_1), .clk(clock_1_out), .dout(out_2));  // open: we, oe, din, be3, be2, be1, be0
  Clock clock_1 (.out(clock_1_out));
endmodule
